# Fritzing sketch OurRobot (saved by Fritzing 0.9.1b)
circuit board: 8.46667cm x 5.64444cm
breadboards: 1

parts:
  Part1 = Arduino Uno (Rev3)
  R1 = Resistor [tolerance=±5% resistance=10k package=THT]
  J1 = Infrared Proximity Sensor
  S1 = Pushbutton [package="[THT]"]
  M1 = DC Motor
  M2 = DC Motor
  DIP-Relay1 = DIP-Relay-D31A [part_number=D31A*]
  DIP-Relay2 = DIP-Relay-D31A [part_number=D31A*]
  VCC1 = 4 x AAA Battery Mount

nets:
  N1: Part1.A0, J1.Vout
  N2: Part1.D8, R1.Pin_1, S1.Pin_3, S1.Pin_4
  N3: Part1.D9_PWM, DIP-Relay2.COIL1_+
  N4: Part1.D10_PWM/SS, DIP-Relay1.COIL1_+, DIP-Relay1.n.c.
  5V: Part1.5V, J1.Vcc, S1.Pin_1, S1.Pin_2
  GND: Part1.GND, R1.Pin_0, J1.GND, DIP-Relay1.Coil2_-, DIP-Relay1.Coil_Sheeld, DIP-Relay2.Coil2_-
  N5: M1.pin_1, DIP-Relay1.B1_Switch_Terminal_B, DIP-Relay1.B2_Switch_Terminal_B
  N6: M1.pin_2, M2.pin_2, VCC1.+
  N7: M2.pin_1, DIP-Relay1.A1_Switch_Terminal_A, DIP-Relay1.A2_Switch_Terminal_A, DIP-Relay2.B2_Switch_Terminal_B, DIP-Relay2.n.c., DIP-Relay2.A2_Switch_Terminal_A, VCC1.-

notes:
  Start/Stop switch
  Sonar sensor
  Left motor
  Right motor
